# Fritzing sketch DDS Generator (saved by Fritzing 0.9.1b)
breadboards: 1

parts:
  AVR328p = Arduino Nano (Rev3.0)
  R1 = Resistor [tolerance=±5% resistance=1.5k package=THT]
  R2 = Resistor [tolerance=±5% resistance=750 package=THT]
  R3 = Resistor [tolerance=±5% resistance=750 package=THT]
  R4 = Resistor [tolerance=±5% resistance=1.5k package=THT]
  R5 = Resistor [tolerance=±5% resistance=750 package=THT]
  R6 = Resistor [tolerance=±5% resistance=750 package=THT]
  R7 = Resistor [tolerance=±5% resistance=750 package=THT]
  R8 = Resistor [tolerance=±5% resistance=750 package=THT]
  R9 = Resistor [tolerance=±5% resistance=750 package=THT]
  R10 = Resistor [tolerance=±5% resistance=1.5k package=THT]
  R11 = Resistor [tolerance=±5% resistance=1.5k package=THT]
  R12 = Resistor [tolerance=±5% resistance=1.5k package=THT]
  R13 = Resistor [tolerance=±5% resistance=1.5k package=THT]
  R14 = Resistor [tolerance=±5% resistance=1.5k package=THT]
  R15 = Resistor [tolerance=±5% resistance=750 package=THT]
  R16 = Resistor [tolerance=±5% resistance=1.5k package=THT]
  C1 = Ceramic Capacitor [capacitance=0.22µF package="100 mil [THT, multilayer]"]
  LCD = LCD screen
  R17 = Trimmer Potentiometer [maximum_resistance=10kΩ package=THT]
  C2 = Ceramic Capacitor [capacitance=470µF package="100 mil [THT, multilayer]"]
  9V_IN = Screw terminal - 2 pins [package=THT]
  Frequency_Up = Pushbutton [package="[THT]"]
  C3 = Ceramic Capacitor [capacitance=0.1µF package="100 mil [THT, multilayer]"]
  Frequency_Down = Pushbutton [package="[THT]"]
  C4 = Ceramic Capacitor [capacitance=0.1µF package="100 mil [THT, multilayer]"]
  Delay_Step = Pushbutton [package="[THT]"]
  C5 = Ceramic Capacitor [capacitance=0.1µF package="100 mil [THT, multilayer]"]
  Select_Wave = Pushbutton [package="[THT]"]
  C6 = Ceramic Capacitor [capacitance=0.1µF package="100 mil [THT, multilayer]"]
  Wave_OUT = Screw terminal - 2 pins [package=THT]
  LM358 = LM 358 Dual Op-Amp [package="DIP8 [THT]"]

nets:
  N1: AVR328p.D1/TX, R1.Pin_0
  N2: AVR328p.D0/RX, R4.Pin_0
  GND: AVR328p.GND, R2.Pin_0, C1.0, LCD.VSS, LCD.R/W, LCD.LED-, R17.leg2, C2.0, 9V_IN.pin2, Frequency_Up.Pin_4, C3.1, Frequency_Down.Pin_3, Frequency_Down.Pin_4, C4.1, Delay_Step.Pin_3, Delay_Step.Pin_4, C5.1, Select_Wave.Pin_3, Select_Wave.Pin_4, C6.1, Wave_OUT.pin2, LM358.connector3
  N3: AVR328p.D2, R10.Pin_0
  N4: AVR328p.D3, R11.Pin_0
  N5: AVR328p.D4, R12.Pin_0
  N6: AVR328p.D5, R13.Pin_0
  N7: AVR328p.D6, R14.Pin_0
  N8: AVR328p.D7, R16.Pin_0
  N9: AVR328p.D8, LCD.DB0
  N10: AVR328p.D9, LCD.DB1
  N11: AVR328p.D10, LCD.DB2
  N12: AVR328p.D11/MOSI, LCD.DB3
  N13: AVR328p.D12/MISO, LCD.E
  N14: AVR328p.VIN, C2.1, 9V_IN.pin1, LM358.connector7
  5V: AVR328p.5V, LCD.VDD, R17.leg1
  N15: AVR328p.A3, Select_Wave.Pin_1, Select_Wave.Pin_2, C6.0
  N16: AVR328p.A2, Delay_Step.Pin_1, Delay_Step.Pin_2, C5.0
  N17: AVR328p.A1, Frequency_Down.Pin_1, Frequency_Down.Pin_2, C4.0
  N18: AVR328p.A0, Frequency_Up.Pin_1, Frequency_Up.Pin_2, C3.0
  N19: AVR328p.3V3, LCD.LED+
  N20: AVR328p.D13/SCK, LCD.RS
  N21: R1.Pin_1, R2.Pin_1, R3.Pin_0
  N22: R3.Pin_1, R4.Pin_1, R5.Pin_0
  N23: R5.Pin_1, R6.Pin_0, R10.Pin_1
  N24: R6.Pin_1, R7.Pin_0, R11.Pin_1
  N25: R7.Pin_1, R8.Pin_0, R12.Pin_1
  N26: R8.Pin_1, R9.Pin_0, R13.Pin_1
  N27: R9.Pin_1, R14.Pin_1, R15.Pin_0
  N28: R15.Pin_1, R16.Pin_1, C1.1, LM358.connector2
  N29: LCD.V0, R17.wiper
  N30: Wave_OUT.pin1, LM358.connector0, LM358.connector1
